# Fritzing sketch tempomatic (saved by Fritzing 0.9.3b)
breadboards: 1

parts:
  M1_-_PC_fan = DC Motor
  R1 = Resistor [tolerance=±5% resistance=220 package=THT]
  R2 = Resistor [tolerance=±20% resistance=10k package=THT]
  4-digit_display_TM1637 = mystery part, 4 pins [chip_label=?]
  Rotary_Encoder = mystery part, 5 pins [chip_label=?]
  DS1 = DS18B20 1-Wire Temperature Sensor [part_number=DS18B20]
  D1 = Rectifier Diode [part_number=1N4007 package="Melf DO-213 AA [SMD]"]
  Q1 = Basic FET N-Channel [part_number=IRF520N package="D2Pak [SMD]"]
  JP1_-_No-name_fan_connector = Header 3 [package=jst-3-pth]
  JP2_-_No-name_fan_connector = Header 3 [package=jst-3-pth]
  M2_-_PC_fan = DC Motor
  Nano = Arduino Nano (Rev3.0)

nets:
  12V: M1_-_PC_fan.pin_1, D1.cathode, JP1_-_No-name_fan_connector.2, JP2_-_No-name_fan_connector.2, M2_-_PC_fan.pin_1, Nano.VIN
  N1: M1_-_PC_fan.pin_2, D1.anode, Q1.drain, JP1_-_No-name_fan_connector.1, JP2_-_No-name_fan_connector.1, M2_-_PC_fan.pin_2
  N2: R1.Pin_1, Nano.D10
  GND: R2.Pin_0, 4-digit_display_TM1637.pin3, Rotary_Encoder.pin4, DS1.GND, Q1.source, Nano.GND
  N3: 4-digit_display_TM1637.pin1, Nano.D9
  N4: 4-digit_display_TM1637.pin2, Nano.D8
  VDD: 4-digit_display_TM1637.pin4, Rotary_Encoder.pin5, DS1.VDD, Nano.5V
  N5: Rotary_Encoder.pin1, Nano.D4
  N6: Rotary_Encoder.pin2, Nano.D2
  N7: DS1.DQ, Nano.D7
