# Fritzing sketch tempomatic (saved by Fritzing 0.9.3b)
breadboards: 1

parts:
  Part1 = Arduino Nano (Rev3.0)
  M1_-_PC_fan = DC Motor
  R1 = Resistor [tolerance=±5% resistance=220 package=THT]
  R2 = Resistor [tolerance=±20% resistance=10k package=THT]
  4-digit_display_TM1637 = mystery part, 4 pins [chip_label=?]
  Rotary_Encoder = mystery part, 5 pins [chip_label=?]
  DS1 = DS18B20 1-Wire Temperature Sensor [part_number=DS18B20]
  D1 = Rectifier Diode [part_number=1N4007 package="Melf DO-213 AA [SMD]"]
  Q1 = Basic FET N-Channel [part_number=IRF520N package="D2Pak [SMD]"]
  JP1_-_No-name_fan_connector = Header 3 [package=jst-3-pth]
  JP2_-_No-name_fan_connector = Header 3 [package=jst-3-pth]
  M2_-_PC_fan = DC Motor

nets:
  GND: Part1.GND, R2.Pin_0, 4-digit_display_TM1637.pin3, Rotary_Encoder.pin4, DS1.GND, Q1.source
  N1: Part1.D2, Rotary_Encoder.pin2
  N2: Part1.D4, Rotary_Encoder.pin1
  N3: Part1.D7, DS1.DQ
  N4: Part1.D8, 4-digit_display_TM1637.pin2
  N5: Part1.D9, 4-digit_display_TM1637.pin1
  N6: Part1.D10, R1.Pin_1
  12V: Part1.VIN, M1_-_PC_fan.pin_1, D1.cathode, JP1_-_No-name_fan_connector.2, JP2_-_No-name_fan_connector.2, M2_-_PC_fan.pin_1
  5V: Part1.5V, 4-digit_display_TM1637.pin4, Rotary_Encoder.pin5, DS1.VDD
  N7: M1_-_PC_fan.pin_2, D1.anode, Q1.drain, JP1_-_No-name_fan_connector.1, JP2_-_No-name_fan_connector.1, M2_-_PC_fan.pin_2
